// Logisim project saguiLongo.circ as structural Verilog: 5 circuits, main circuit main
module main (
);

  wire Clk, I_type, jumpPC, memToReg, memWrite, not_1_out, regWrite;
  wire [1:0] undriven, undriven_2;
  wire [7:0] adder_1_out, ctrl_type_fu_1_pc_out, multiplexer_1_out, multiplexer_2_out, multiplexer_3_out,
       PC_q, ram_1_dout, undriven_3;

  Multiplexer #(.width(8)) multiplexer_1 (.in0(8'h4), .in1(ctrl_type_fu_1_pc_out), .out(multiplexer_1_out), .sel(1'b0));
  Adder adder_1 (.a(PC_q), .b(multiplexer_1_out), .out(adder_1_out), .cin(1'b0));  // open: cout
  Multiplexer #(.width(8)) multiplexer_2 (
    .in0(adder_1_out), .in1(ctrl_type_fu_1_pc_out), .out(multiplexer_2_out), .sel(1'b0));
  // AND_Gate and_1 has open pins: in0=jumpPC, in1=I_type, out=open
  Register PC (.D(multiplexer_2_out), .en(1'b1), .clk(Clk), .Q(PC_q), .clr(1'b0));
  // ROM #(.line("quad")) rom_1: pin names not known; wires that end beside it: PC_q
  Clock clock_Global (.out(Clk));
  BancoRegistradores bancoregistradores_1 (
    .WE(regWrite), .write_data(multiplexer_3_out), .clk(Clk), .a_adress(undriven_2), .b_adress(undriven));  // open: a_data, b_data
  Arithmetic_type_FU arithmetic_type_fu_1 ();  // open: a, b, selector, result
  Arithmetic_type_FU arithmetic_type_fu_2 ();  // open: a, b, selector, result
  Data_type_FU data_type_fu_1 ();  // open: a, b, selector, result
  Ctrl_type_FU ctrl_type_fu_1 (.PC_out(ctrl_type_fu_1_pc_out));  // open: a, b, PC_in, selector
  RAM #(.asyncread("true")) ram_1 (
    .addr(undriven_3), .we(memWrite), .oe(not_1_out), .clk(Clk), .dout(ram_1_dout));  // open: din
  not not_1 (not_1_out, memWrite);
  Multiplexer #(.width(8)) multiplexer_3 (.in0(undriven_3), .in1(ram_1_dout), .out(multiplexer_3_out), .sel(memToReg));

  // Notes on the sheet:
  //   Somador
  //   Memoria de Instrucoes
  //   Memoria de Dados
endmodule

module Data_type_FU (
  input  [7:0] a,
  input  [7:0] b,
  input  [1:0] selector,
  output [7:0] result
);

  wire [3:0] bit_extender_1_out;

  Bit_Extender #(.out_width(4)) bit_extender_1 (.in(b), .out(bit_extender_1_out));
  Multiplexer #(.select(2), .width(8)) multiplexer_1 (
    .in0({bit_extender_1_out, a[3:0]}), .in1({a[7:4], bit_extender_1_out}), .in2(b), .in3({8{1'b0}}),
    .out(result), .sel(selector));

  // Notes on the sheet:
  //   Move High
  //   Move Low
  //   Ld/St address
endmodule

module Ctrl_type_FU (
  input  [7:0] a,
  input  [7:0] b,
  input  [7:0] PC_in,
  input  [1:0] selector,
  output [7:0] PC_out
);

  wire isZero;
  wire [7:0] adder_1_out, multiplexer_1_out, multiplexer_2_out;

  nor nor_1 (isZero, a[0], a[1], a[2], a[3], a[5], a[6], a[7], a[4]);
  Adder adder_1 (.a(b), .b(PC_in), .out(adder_1_out), .cin(1'b0));  // open: cout
  Multiplexer #(.width(8)) multiplexer_1 (.in0(PC_in), .in1(b), .out(multiplexer_1_out), .sel(isZero));
  Multiplexer #(.width(8)) multiplexer_2 (.in0(PC_in), .in1(adder_1_out), .out(multiplexer_2_out), .sel(isZero));
  Multiplexer #(.select(2), .width(8)) multiplexer_3 (
    .in0(b), .in1(adder_1_out), .in2(multiplexer_1_out), .in3(multiplexer_2_out), .out(PC_out), .sel(selector));

  // Notes on the sheet:
  //   PC + Imm
  //   Jump Register
  //   Jump Immediate
  //   Branch On Zero Register
  //   Branch On Zero
endmodule

module Arithmetic_type_FU (
  input  [7:0] a,
  input  [7:0] b,
  input  [2:0] selector,
  output [7:0] result
);

  wire or_2_out;
  wire [7:0] adder_1_out, and_1_out, multiplexer_1_out, multiplexer_2_out, not_1_out, or_1_out,
       shifter_1_out, shifter_2_out, subtractor_1_out;

  Adder adder_1 (.a(a), .b(b), .out(adder_1_out), .cin(1'b0));  // open: cout
  Subtractor subtractor_1 (.a(a), .b(b), .out(subtractor_1_out), .bin(1'b0));  // open: bout
  assign and_1_out = a & b;  // AND_Gate and_1, 8 bits wide
  assign or_1_out = a | b;  // OR_Gate or_1, 8 bits wide
  assign not_1_out = ~b;  // NOT_Gate not_1, 8 bits wide
  Shifter shifter_1 (.in(a), .\dist (b[2:0]), .out(shifter_1_out));
  Shifter #(.shift("lr")) shifter_2 (.in(a), .\dist (b[2:0]), .out(shifter_2_out));
  Multiplexer #(.width(8)) multiplexer_1 (
    .in0(shifter_1_out), .in1({8{1'b0}}), .out(multiplexer_1_out), .sel(or_2_out));
  Multiplexer #(.width(8)) multiplexer_2 (
    .in0(shifter_2_out), .in1({8{1'b0}}), .out(multiplexer_2_out), .sel(or_2_out));
  or or_2 (or_2_out, b[7], b[6], b[5], b[4], b[3]);
  Multiplexer #(.select(3), .width(8)) multiplexer_3 (
    .in0(adder_1_out), .in1(subtractor_1_out), .in2(and_1_out), .in3(or_1_out), .in4(not_1_out),
    .in5(multiplexer_1_out), .in6(multiplexer_2_out), .in7({8{1'b0}}), .out(result), .sel(selector));

  // Notes on the sheet:
  //   Somador
  //   Subtrator
  //   And
  //   Or
  //   Not
  //   Logical Shifter Left
  //   Logical Shifter Right
endmodule

module BancoRegistradores (
  input  WE,
  input  [7:0] write_data,
  input  clk,
  input  [1:0] a_adress,
  input  [1:0] b_adress,
  output [7:0] a_data,
  output [7:0] b_data
);

  wire demultiplexer_1_out0, demultiplexer_1_out1, demultiplexer_1_out2, demultiplexer_1_out3;
  wire [7:0] register_1_q, register_2_q, register_3_q, register_4_q;

  Demultiplexer #(.select(2)) demultiplexer_1 (
    .out0(demultiplexer_1_out0), .out1(demultiplexer_1_out1), .out2(demultiplexer_1_out2),
    .out3(demultiplexer_1_out3), .in(WE), .sel(a_adress));
  Register register_1 (.D(write_data), .en(demultiplexer_1_out0), .clk(clk), .Q(register_1_q), .clr(1'b0));
  Register register_2 (.D(write_data), .en(demultiplexer_1_out1), .clk(clk), .Q(register_2_q), .clr(1'b0));
  Register register_3 (.D(write_data), .en(demultiplexer_1_out2), .clk(clk), .Q(register_3_q), .clr(1'b0));
  Register register_4 (.D(write_data), .en(demultiplexer_1_out3), .clk(clk), .Q(register_4_q), .clr(1'b0));
  Multiplexer #(.select(2), .width(8)) multiplexer_1 (
    .in0(register_1_q), .in1(register_2_q), .in2(register_3_q), .in3(register_4_q), .out(a_data),
    .sel(a_adress));
  Multiplexer #(.select(2), .width(8)) multiplexer_2 (
    .in0(register_1_q), .in1(register_2_q), .in2(register_3_q), .in3(register_4_q), .out(b_data),
    .sel(b_adress));
endmodule
